# Fritzing sketch Circuit (saved by Fritzing 0.9.3b)

parts:
  CHARGER1 = USB_LiIon_LiPoly_Charger_v1.2
  Componente10 = PowerBoost 500 Basic
  Componente11 = Arduino Nano (Rev3.0)
  SONAR1 = Maxbotix MaxSonar Ultrasonic Sensor
  SONAR2 = Maxbotix MaxSonar Ultrasonic Sensor
  SONAR3 = Maxbotix MaxSonar Ultrasonic Sensor
  U1 = Vibration Motor- ROB-08449 [package=vibe-motor-10mm]
  U2 = Vibration Motor- ROB-08449 [package=vibe-motor-10mm]
  U3 = Vibration Motor- ROB-08449 [package=vibe-motor-10mm]
  U4 = LIPO-110mAh [package=lipo-110]
  Componente12 = Solar Cell
  Componente13 = Solar Cell
  S1 = Pushbutton [package=THT]

nets:
  N1: CHARGER1.batt_minus_1, U4.-
  N2: CHARGER1.batt_plus_1, U4.+
  N3: CHARGER1.load_minus_1, S1.leg0
  GND: CHARGER1.load_plus_1, Componente10.GND, Componente11.GND, SONAR1.GND, SONAR1.BW, SONAR2.GND, SONAR3.GND, U1.+, U2.+, U3.+
  N4: Componente10.VBAT, S1.leg1
  +5V: Componente10.5.0V, Componente11.5V, SONAR1.+5V, SONAR2.+5V, SONAR3.+5V
  N5: Componente11.D5, SONAR1.PW
  N6: Componente11.D6, U3.-
  N7: Componente11.D7, U2.-
  N8: Componente11.D10, SONAR2.PW
  N9: Componente11.D11/MOSI, U1.-
  N10: Componente11.D12/MISO, SONAR3.PW
  N11: Componente12.+, Componente13.+
  N12: Componente12.-, Componente13.-

custom parts:
  PowerBoost 500 Basic: The PowerBoost 500 Basic is a little DC/DC boost converter module that can run from 1.8V batteries or higher, and convert the battery output to 5.2V DC for running your 5V projects. At its heart is a TPS61090 boost converter from TI. This boost converter chip has some really nice extras such as low battery detection, 2A internal switch, synchronous conversion, excellent efficiency, and 700KHz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
  Maxbotix MaxSonar Ultrasonic Sensor: Maxbotix MaxSonar Ultrasonic Sensor LV-EZ0, LV-EZ1, LV-EZ2, LV-EZ3, LV-EZ4
